# Fritzing sketch smart_alarm (saved by Fritzing 1.0.8)
circuit board: 6.48406cm x 2.99458cm
breadboards: 1

parts:
  R8 = Resistor [tolerance=±5% resistance=270 power=0.25W package=THT]
  C8 = Ceramic Capacitor [capacitance=10nF voltage=35V package="100 mil [THT, multilayer]"]
  R11 = Resistor [tolerance=±5% resistance=150 power=0.25W package=THT]
  C10 = Electrolytic Capacitor [capacitance=1µF voltage=35V package="100 mil [THT, electrolytic]"]
  C11 = Electrolytic Capacitor [capacitance=1µF voltage=35V package="100 mil [THT, electrolytic]"]
  PR1 = Photocell (LDR) [power=0.25W dark_resistance_@0.01lx=300kΩ light_resistance_@100lx=400Ω luminance=10lx package=THT]  # not connected
  R13 = Resistor [tolerance=±5% power=0.25W resistance=1k package=THT]
  R9 = Resistor [tolerance=±5% power=0.25W resistance=270 package=THT]
  C9 = Ceramic Capacitor [capacitance=10nF voltage=35V package="100 mil [THT, multilayer]"]
  J1 = female pin header, 20 pins [form="♀ (female)"]
  J2 = female pin header, 20 pins [form="♀ (female)"]
  R12 = Resistor [tolerance=±5% power=0.25W resistance=10k package=THT]
  C12 = Ceramic Capacitor [capacitance=100nF voltage=35V package="100 mil [THT, multilayer]"]
  C13 = Electrolytic Capacitor [capacitance=1µF voltage=35V package="100 mil [THT, electrolytic]"]
  5v = female pin header, 1 pin [form="♀ (female)"]
  Left = female pin header, 1 pin [form="♀ (female)"]
  + = female pin header, 1 pin [form="♀ (female)"]
  - = female pin header, 1 pin [form="♀ (female)"]
  +_2 = female pin header, 1 pin [form="♀ (female)"]
  -_2 = female pin header, 1 pin [form="♀ (female)"]
  gnd = female pin header, 1 pin [form="♀ (female)"]
  Right = female pin header, 1 pin [form="♀ (female)"]
  SDA = female pin header, 1 pin [form="♀ (female)"]
  SCK = female pin header, 1 pin [form="♀ (female)"]
  3_3V = female pin header, 1 pin [form="♀ (female)"]
  GND = female pin header, 1 pin [form="♀ (female)"]
  GND_2 = female pin header, 1 pin [form="♀ (female)"]
  R10 = Resistor [tolerance=±5% power=0.25W resistance=150 package=THT]
  GND_3 = female pin header, 1 pin [form="♀ (female)"]
  DI = female pin header, 1 pin [form="♀ (female)"]
  CI = female pin header, 1 pin [form="♀ (female)"]
  5V = female pin header, 1 pin [form="♀ (female)"]
  snooze = female pin header, 1 pin [form="♀ (female)"]
  snooze_2 = female pin header, 1 pin [form="♀ (female)"]
  spk_+ = female pin header, 1 pin [form="♀ (female)"]
  spk_- = female pin header, 1 pin [form="♀ (female)"]
  spk_+_2 = female pin header, 1 pin [form="♀ (female)"]
  spk_-_2 = female pin header, 1 pin [form="♀ (female)"]
  S1 = SWITCH-MOMENTARY-2 [package=tactile-pth-12mm]  # not connected
  pr1 = female pin header, 1 pin [form="♀ (female)"]
  pr1_2 = female pin header, 1 pin [form="♀ (female)"]

nets:
  N1: R8.Pin_0, J2.pin17
  N2: R8.Pin_1, C8.0, C11.+, R10.Pin_0
  N3: C8.1, R11.Pin_0, C9.0, J1.pin3, J1.pin15, J2.pin13, J2.pin20, R12.Pin_1, C13.-, gnd.pin1, GND_2.pin1, R10.Pin_1, GND_3.pin1
  N4: R11.Pin_1, C10.+, R9.Pin_1, C9.1
  N5: C10.-, Right.pin1
  N6: C11.-, Left.pin1
  N7: R13.Pin_0, J1.pin9, C12.0, snooze_2.pin1
  N8: R13.Pin_1, J2.pin9, pr1_2.pin1
  N9: R9.Pin_0, J1.pin16
  N10: J1.pin1, 5v.pin1
  N11: J1.pin2, 5V.pin1
  N12: J1.pin19, C13.+, pr1.pin1
  N13: J2.pin1, 3_3V.pin1
  N14: J2.pin2, SDA.pin1
  N15: J2.pin3, SCK.pin1
  N16: J2.pin5, GND.pin1
  N17: J2.pin10, DI.pin1
  N18: J2.pin12, CI.pin1
  N19: R12.Pin_0, C12.1, snooze.pin1
  N20: +.pin1, spk_+.pin1
  N21: -.pin1, spk_-.pin1
  N22: +_2.pin1, spk_+_2.pin1
  N23: -_2.pin1, spk_-_2.pin1

notes:
  for the switch which will be off-board
  the header pins are for the pcb holes where the amp module will 'plug' into.
  to photo resistor
  to pcb header
  snooze/stop
  pr1
  sw1
  SSD 1306
  DISPLAY
  PAM 8403
  APA102C
  GND
  DI
  CI
  5V
  3.3v
  SCK
  SDA
  +
  -
  APA102C LEDS
  3.3V
