# Fritzing sketch smart_alarm_V2.0 (saved by Fritzing 1.0.8)
circuit board: 6.48406cm x 2.99458cm
breadboards: 1

parts:
  R8 = Resistor [tolerance=±5% resistance=270 power=0.25W package=THT]
  C8 = Ceramic Capacitor [capacitance=10nF voltage=35V package="100 mil [THT, multilayer]"]
  R11 = Resistor [tolerance=±5% resistance=150 power=0.25W package=THT]
  C10 = Electrolytic Capacitor [capacitance=1µF voltage=35V package="100 mil [THT, electrolytic]"]
  C11 = Electrolytic Capacitor [capacitance=1µF voltage=35V package="100 mil [THT, electrolytic]"]
  R13 = Resistor [tolerance=±5% power=0.25W resistance=1k package=THT]
  R9 = Resistor [tolerance=±5% power=0.25W resistance=270 package=THT]
  C9 = Ceramic Capacitor [capacitance=10nF voltage=35V package="100 mil [THT, multilayer]"]
  R12 = Resistor [tolerance=±5% power=0.25W resistance=10k package=THT]
  C12 = Ceramic Capacitor [capacitance=100nF voltage=35V package="100 mil [THT, multilayer]"]
  C13 = Electrolytic Capacitor [capacitance=1µF voltage=35V package="100 mil [THT, electrolytic]"]
  5v = female pin header, 1 pin [form="♀ (female)"]
  Left = female pin header, 1 pin [form="♀ (female)"]
  - = female pin header, 1 pin [form="♀ (female)"]
  + = female pin header, 1 pin [form="♀ (female)"]
  -_2 = female pin header, 1 pin [form="♀ (female)"]
  gnd = female pin header, 1 pin [form="♀ (female)"]
  Right = female pin header, 1 pin [form="♀ (female)"]
  SDA = female pin header, 1 pin [form="♀ (female)"]
  SCK = female pin header, 1 pin [form="♀ (female)"]
  3_3V = female pin header, 1 pin [form="♀ (female)"]
  GND = female pin header, 1 pin [form="♀ (female)"]
  GND_2 = female pin header, 1 pin [form="♀ (female)"]
  R10 = Resistor [tolerance=±5% power=0.25W resistance=150 package=THT]
  GND_3 = female pin header, 1 pin [form="♀ (female)"]
  DI = female pin header, 1 pin [form="♀ (female)"]
  CI = female pin header, 1 pin [form="♀ (female)"]
  5V = female pin header, 1 pin [form="♀ (female)"]
  pr1 = female pin header, 1 pin [form="♀ (female)"]
  pr1_2 = female pin header, 1 pin [form="♀ (female)"]
  snooze = female pin header, 1 pin [form="♀ (female)"]
  snooze_2 = female pin header, 1 pin [form="♀ (female)"]
  spk_+ = female pin header, 1 pin [form="♀ (female)"]
  spk_- = female pin header, 1 pin [form="♀ (female)"]
  spk_+_2 = female pin header, 1 pin [form="♀ (female)"]
  spk_-_2 = female pin header, 1 pin [form="♀ (female)"]
  +_2 = female pin header, 1 pin [form="♀ (female)"]
  J2 = female pin header, 20 pins [form="♀ (female)"]
  J1 = female pin header, 20 pins [form="♀ (female)"]

nets:
  N1: R8.Pin_0, J2.pin17
  N2: R8.Pin_1, C8.0, C11.+, R10.Pin_0
  GND: C8.1, R11.Pin_0, C9.0, R12.Pin_1, C13.-, gnd.pin1, GND_2.pin1, R10.Pin_1, GND_3.pin1, J2.pin20, J1.pin3
  N3: R11.Pin_1, C10.+, R9.Pin_1, C9.1
  N4: C10.-, Right.pin1
  N5: C11.-, Left.pin1
  N6: R13.Pin_0, C12.0, snooze.pin1
  N7: R13.Pin_1, pr1.pin1, J2.pin9
  N8: R9.Pin_0, J1.pin16
  N9: R12.Pin_0, C12.1, snooze_2.pin1, J1.pin9
  N10: C13.+, pr1_2.pin1, J1.pin19
  N11: 5v.pin1, J1.pin1
  N12: -.pin1, spk_-.pin1
  N13: +.pin1, spk_+_2.pin1
  N14: -_2.pin1, spk_-_2.pin1
  N15: SDA.pin1, J2.pin2
  N16: SCK.pin1, J2.pin3
  N17: 3_3V.pin1, J2.pin1
  N18: GND.pin1, J2.pin5
  N19: DI.pin1, J2.pin10
  N20: CI.pin1, J2.pin12
  N21: 5V.pin1, J1.pin2
  N22: spk_+.pin1, +_2.pin1
  N23: J2.pin13, J1.pin15

notes:
  for the switch which will be off-board
  the header pins are for the pcb holes where the amp module will 'plug' into.
  to photo resistor
  snooze/stop
  pr1
  sw1
  SSD 1306
  DISPLAY
  PAM 8403
  APA102C
  GND
  DI
  CI
  5V
  3.3v
  SCK
  SDA
  +
  -
  APA102C LEDS
  3.3V
  PAM8403
  to PAM8403 inputs
