# Fritzing sketch amp_pwm_audioMod (saved by Fritzing 1.0.7)
breadboards: 1

parts:
  SP1 = SPEAKER [package=pcb_mount_speaker]
  R8 = Resistor [tolerance=±5% resistance=270 power=0.25W package=THT]
  R9 = Resistor [tolerance=±5% resistance=270 power=0.25W package=THT]
  C8 = Ceramic Capacitor [capacitance=10nF voltage=35V package="100 mil [THT, multilayer]"]
  C9 = Ceramic Capacitor [capacitance=10nF voltage=35V package="100 mil [THT, multilayer]"]
  R10 = Resistor [tolerance=±5% resistance=150 power=0.25W package=THT]
  R11 = Resistor [tolerance=±5% resistance=150 power=0.25W package=THT]
  C10 = Electrolytic Capacitor [capacitance=1µF voltage=35V package="100 mil [THT, electrolytic]"]
  C11 = Electrolytic Capacitor [capacitance=1µF voltage=35V package="100 mil [THT, electrolytic]"]
  AMP1 = PAM8403 6W Stereo Amplifier
  MCU1 = Raspberry Pi Zero
  SP2 = SPEAKER [package=pcb_mount_speaker]

nets:
  N1: SP1.+, AMP1.LOUT-
  N2: SP1.-, AMP1.LOUT+
  N3: R8.Pin_0, MCU1.pin_33
  N4: R8.Pin_1, C8.0, R10.Pin_0, C11.+
  N5: R9.Pin_0, MCU1.pin_12
  N6: R9.Pin_1, C9.1, R11.Pin_1, C10.+
  N7: C8.1, C9.0, R10.Pin_1, R11.Pin_0, AMP1.INPUTG, MCU1.pin_6, MCU1.pin_9, MCU1.pin_39
  N8: C10.-, AMP1.INPUTR
  N9: C11.-, AMP1.INPUTL
  N10: AMP1.ROUT-, SP2.+
  N11: AMP1.ROUT+, SP2.-
  N12: AMP1.POWER-, MCU1.pin_32
  N13: AMP1.POWER+, MCU1.pin_2

custom parts:
  PAM8403 6W Stereo Amplifier: PAM8403 6 Watt Stereo Amplifier
