# Fritzing sketch complete circuit (saved by Fritzing 1.0.7)
breadboards: 1

parts:
  SP1 = SPEAKER [package=pcb_mount_speaker]
  R8 = Resistor [tolerance=±5% resistance=270 power=0.25W package=THT]
  C8 = Ceramic Capacitor [capacitance=10nF voltage=35V package="100 mil [THT, multilayer]"]
  R10 = Resistor [tolerance=±5% resistance=150 power=0.25W package=THT]
  R11 = Resistor [tolerance=±5% resistance=150 power=0.25W package=THT]
  C10 = Electrolytic Capacitor [capacitance=1µF voltage=35V package="100 mil [THT, electrolytic]"]
  C11 = Electrolytic Capacitor [capacitance=1µF voltage=35V package="100 mil [THT, electrolytic]"]
  S3 = Momentary Switch [package=ksa_sealed_tac_switch]
  R12 = Resistor [tolerance=±5% resistance=10k power=0.25W package=THT]
  R14 = Photocell (LDR) [power=0.25W dark_resistance_@0.01lx=300kΩ light_resistance_@100lx=400Ω luminance=10lx package=THT]
  SP2 = SPEAKER [package=pcb_mount_speaker]
  OLED_I2C1 = OLED 128x64 I2C Monochrome Display
  AMP1 = PAM8403
  C13 = Ceramic Capacitor [capacitance=1µF voltage=35V package="0603 [SMD, multilayer]"]
  C12 = Ceramic Capacitor [capacitance=100nF voltage=35V package="100 mil [THT, multilayer]"]
  R13 = Resistor [tolerance=±5% power=0.25W resistance=1k package=THT]
  Raspberry_Pi_Zero_2W = Raspberry Pi Zero
  R9 = Resistor [tolerance=±5% power=0.25W resistance=270 package=THT]
  C9 = Ceramic Capacitor [capacitance=10nF voltage=35V package="100 mil [THT, multilayer]"]

nets:
  N1: SP1.+, AMP1.connector4
  N2: SP1.-, AMP1.connector3
  N3: R8.Pin_0, Raspberry_Pi_Zero_2W.pin_33
  N4: R8.Pin_1, C8.0, R10.Pin_0, C11.+
  N5: C8.1, R10.Pin_1, R11.Pin_0, R12.Pin_1, OLED_I2C1.connector8, AMP1.connector5, AMP1.connector8, C13.0, Raspberry_Pi_Zero_2W.pin_6, Raspberry_Pi_Zero_2W.pin_9, Raspberry_Pi_Zero_2W.pin_30, Raspberry_Pi_Zero_2W.pin_39, C9.0
  N6: R11.Pin_1, C10.+, R9.Pin_1, C9.1
  N7: C10.-, AMP1.connector9
  N8: C11.-, AMP1.connector7
  N9: S3.1, S3.2, C12.0, R13.Pin_0
  N10: S3.3, S3.4, R12.Pin_0, C12.1, Raspberry_Pi_Zero_2W.pin_18
  N11: R14.pin_0, C13.1, Raspberry_Pi_Zero_2W.pin_38
  N12: R14.pin_1, OLED_I2C1.connector7, R13.Pin_1, Raspberry_Pi_Zero_2W.pin_1, Raspberry_Pi_Zero_2W.pin_17
  N13: SP2.+, AMP1.connector1
  N14: SP2.-, AMP1.connector2
  N15: OLED_I2C1.connector4, Raspberry_Pi_Zero_2W.pin_3
  N16: OLED_I2C1.connector5, Raspberry_Pi_Zero_2W.pin_5
  N17: AMP1.connector6, Raspberry_Pi_Zero_2W.pin_2
  N18: Raspberry_Pi_Zero_2W.pin_32, R9.Pin_0
